# Fritzing sketch MultiSCD30 (saved by Fritzing 0.9.7b)
breadboards: 1

parts:
  MICROCONTROLLER = Arduino Nano (Rev3.0)
  LOGIC_CONVERTER = I2C level shifter bidirectional
  SENSOR#3 = SCD30
  SENSOR#2 = SCD30
  SENSOR#1 = SCD30
  SENSOR#0 = SCD30
  I2C_MULTIPLEXER = Adafruit TCA9548A
  RTC_MODULE = ZS-042 RTC Module
  R1 = Resistor [tolerance=±5% power=0.25 resistance=5k package=THT]
  R2 = Resistor [tolerance=±5% power=0.25 resistance=5k package=THT]

nets:
  GND: MICROCONTROLLER.GND, LOGIC_CONVERTER.GND, SENSOR#3.GND, SENSOR#2.GND, SENSOR#1.GND, SENSOR#0.GND, I2C_MULTIPLEXER.GND, RTC_MODULE.GND
  5V: MICROCONTROLLER.5V, LOGIC_CONVERTER.HV
  SCL_5V: MICROCONTROLLER.A5, LOGIC_CONVERTER.HV2
  SDA_5V: MICROCONTROLLER.A4, LOGIC_CONVERTER.HV1
  3.3V: MICROCONTROLLER.3V3, LOGIC_CONVERTER.LV, SENSOR#3.VDD, SENSOR#2.VDD, SENSOR#1.VDD, SENSOR#0.VDD, I2C_MULTIPLEXER.VCC, RTC_MODULE.VCC, R1.Pin_1, R2.Pin_1
  SCL_3V: LOGIC_CONVERTER.LV2, I2C_MULTIPLEXER.INPUTSCL, R2.Pin_0
  SDA_3V: LOGIC_CONVERTER.LV1, I2C_MULTIPLEXER.INPUTSDA, R1.Pin_0
  SCL#3: SENSOR#3.TX/SCL, I2C_MULTIPLEXER.3SCL
  SDA#3: SENSOR#3.RX/SDA, I2C_MULTIPLEXER.3SDA
  SCL#2: SENSOR#2.TX/SCL, I2C_MULTIPLEXER.2SCL
  SDA#2: SENSOR#2.RX/SDA, I2C_MULTIPLEXER.2SDA
  SCL#1: SENSOR#1.TX/SCL, I2C_MULTIPLEXER.1SCL
  SDA#1: SENSOR#1.RX/SDA, I2C_MULTIPLEXER.1SDA
  SCL#0: SENSOR#0.TX/SCL, I2C_MULTIPLEXER.0SCL
  SDA#0: SENSOR#0.RX/SDA, I2C_MULTIPLEXER.0SDA
  SDA#4: I2C_MULTIPLEXER.4SDA, RTC_MODULE.SDA
  SCL#4: I2C_MULTIPLEXER.4SCL, RTC_MODULE.SCL

custom parts:
  SCD30: CO2 , humidity, and temperature sensor * Current consumption: 19 mA @ 1 meas. per 2 s. * Digital interface UART or I2C * Company: Sensirion - The Sensor Company Electrical specifications * average current: 19 mA * max. current: 75 mA * DC supply: 3.3 V - 5.5 V Operation conditions * temperature: 0 – 50°C * humidity: 0 – 95 %RH * sensor lifetime: 15 years CO2-sensor: * NDIR CO 2 sensor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
  Adafruit TCA9548A: You just found the perfect I2C sensor, and you want to wire up two or three or more of them to your Arduino when you realize "Uh oh, this chip has a fixed I2C address, and from what I know about I2C, you cannot have two devices with the same address on the same SDA/SCL pins!" Are you out of luck? You would be, if you didn't have this ultra-cool TCA9548A 1-to-8 I2C multiplexer! Finally, a way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
