# Fritzing sketch ArduinoVersion-Fritzing (saved by Fritzing 0.9.7b)
breadboards: 1

parts:
  MICROCONTROLLER = Arduino Nano (Rev3.0)
  LEVEL_CONVERTER_FOR_SPI = I2C level shifter bidirectional
  LEVEL_CONVERTER_FOR_I2C = I2C level shifter bidirectional
  CAPACITOR_1 = Ceramic Capacitor [capacitance=470nF voltage=35V package="200 mil [THT, multilayer]"]
  CAPACITOR_2 = Ceramic Capacitor [capacitance=470nF voltage=35V package="200 mil [THT, multilayer]"]
  TOGGLE_SWITCH = Toggle Switch [package=THT]
  R1 = Resistor [tolerance=±5% power=0.25 resistance=330 package=THT]
  R3 = Resistor [tolerance=±5% power=0.25 resistance=1k package=THT]
  LED_INDICATOR = smd LED [color="Red (633nm)" package="0805 [SMD]"]
  CO2_SENSOR = SCD30
  CLOCK_MODULE = ZS-042 RTC Module
  STORAGE_MODULE = MicroSD Card Module
  R3_2 = Resistor [tolerance=±5% resistance=4.7k package="0603 [SMD]"]
  ANEMOMETER_CONNECTOR = RJ45 Jack [package=rj45-8]

nets:
  GND: MICROCONTROLLER.GND, LEVEL_CONVERTER_FOR_SPI.GND, LEVEL_CONVERTER_FOR_I2C.GND, CAPACITOR_1.0, CAPACITOR_2.0, R3.Pin_0, LED_INDICATOR.cathode, CO2_SENSOR.GND, CLOCK_MODULE.GND, STORAGE_MODULE.GND, ANEMOMETER_CONNECTOR.3
  WIND_SPEED: MICROCONTROLLER.D2, R3_2.Pin_0, ANEMOMETER_CONNECTOR.4
  SWITCH: MICROCONTROLLER.D5, TOGGLE_SWITCH.L2
  LED: MICROCONTROLLER.D6, R1.Pin_0
  CS 5V: MICROCONTROLLER.D10, LEVEL_CONVERTER_FOR_SPI.HV2
  MOSI 5V: MICROCONTROLLER.D11/MOSI, LEVEL_CONVERTER_FOR_SPI.HV4
  MISO: MICROCONTROLLER.D12/MISO, STORAGE_MODULE.MISO
  5V: MICROCONTROLLER.5V, LEVEL_CONVERTER_FOR_SPI.HV, LEVEL_CONVERTER_FOR_I2C.HV, CO2_SENSOR.VDD, STORAGE_MODULE.VCC, R3_2.Pin_1, ANEMOMETER_CONNECTOR.1
  SCL 5V: MICROCONTROLLER.A5, LEVEL_CONVERTER_FOR_I2C.HV3
  SDA 5V: MICROCONTROLLER.A4, LEVEL_CONVERTER_FOR_I2C.HV4
  WIND_DIR: MICROCONTROLLER.A3, ANEMOMETER_CONNECTOR.2
  3.3V: MICROCONTROLLER.3V3, LEVEL_CONVERTER_FOR_SPI.LV, LEVEL_CONVERTER_FOR_I2C.LV, CAPACITOR_1.1, CAPACITOR_2.1, CLOCK_MODULE.VCC
  SCK 5V: MICROCONTROLLER.D13/SCK, LEVEL_CONVERTER_FOR_SPI.HV3
  MOSI 3.3V: LEVEL_CONVERTER_FOR_SPI.LV4, STORAGE_MODULE.MOSI
  SCK 3.3V: LEVEL_CONVERTER_FOR_SPI.LV3, STORAGE_MODULE.SCK
  CS 3.3V: LEVEL_CONVERTER_FOR_SPI.LV2, STORAGE_MODULE.CS
  SDA 3.3V: LEVEL_CONVERTER_FOR_I2C.LV4, CO2_SENSOR.RX/SDA, CLOCK_MODULE.SDA
  SCL 3.3V: LEVEL_CONVERTER_FOR_I2C.LV3, CO2_SENSOR.TX/SCL, CLOCK_MODULE.SCL
  N1: TOGGLE_SWITCH.COM, R3.Pin_1
  N2: R1.Pin_1, LED_INDICATOR.anode

custom parts:
  SCD30: CO2 , humidity, and temperature sensor * Current consumption: 19 mA @ 1 meas. per 2 s. * Digital interface UART or I2C * Company: Sensirion - The Sensor Company Electrical specifications * average current: 19 mA * max. current: 75 mA * DC supply: 3.3 V - 5.5 V Operation conditions * temperature: 0 – 50°C * humidity: 0 – 95 %RH * sensor lifetime: 15 years CO2-sensor: * NDIR CO 2 sensor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
  RJ45 Jack: RJ45 Jack Simple RJ45, 8-pin connection - connector for common Cat5, Cat5e, and Cat6 Ethernet cables. Footprint not yet proven in production. Connector sku is PRT-00643; Breakout PCB sku is BOB-00716.
